// Digital circuit ter_adder_4bit.dig as structural Verilog
module ter_adder_4bit (
  input  A0a,
  input  B0a,
  input  A0b,
  input  B0b,
  input  A1a,
  input  B1a,
  input  A1b,
  input  B1b,
  input  A2a,
  input  B2a,
  input  A2b,
  input  B2b,
  input  A3a,
  input  B3a,
  input  A3b,
  input  B3b,
  input  n0,
  input  n1,
  output S0_1,
  output S0_0,
  output S1_0,
  output S1_1,
  output S2_1,
  output S2_0,
  output S3_0,
  output S3_1,
  output S4_0,
  output S4_1
);

  wire add_1_c_o, add_1_s, add_2_c_o, add_2_s, add_3_c_o, add_3_s, add_4_s;

  Add #(.Bits(1)) add_1 (.a(A0a), .b(B0a), .c_i(A0b), .s(add_1_s), .c_o(add_1_c_o));
  Add #(.Bits(1)) add_2 (.a(A1a), .b(B1a), .c_i(A1b), .s(add_2_s), .c_o(add_2_c_o));
  Add #(.Bits(1)) add_3 (.a(A2a), .b(B2a), .c_i(A2b), .s(add_3_s), .c_o(add_3_c_o));
  Add #(.Bits(1)) add_4 (.a(A3a), .b(B3a), .c_i(A3b), .s(add_4_s), .c_o(S4_1));
  Add #(.Bits(1)) add_5 (.a(n1), .b(add_1_s), .c_i(B0b), .s(S0_1), .c_o(S1_0));
  Add #(.Bits(1)) add_6 (.a(add_1_c_o), .b(add_2_s), .c_i(B1b), .s(S1_1), .c_o(S2_0));
  Add #(.Bits(1)) add_7 (.a(add_2_c_o), .b(add_3_s), .c_i(B2b), .s(S2_1), .c_o(S3_0));
  Add #(.Bits(1)) add_8 (.a(add_3_c_o), .b(add_4_s), .c_i(B3b), .s(S3_1), .c_o(S4_0));

  assign S0_0 = n0;
endmodule

/* Test case:
A0a B0a A0b B0b A1a B1a A1b B1b A2a B2a A2b B2b A3a B3a A3b B3b n0 n1 S0_1 S0_0 S1_0 S1_1 S2_1 S2_0 S3_0 S3_1 S4_0 S4_1
0 0 1 1 0 0 1 1 0 0 1 1 0 0 1 1 0 1 1 0 1 0 0 1 1 0 1 0
1 0 1 1 1 0 1 1 1 0 1 1 0 1 1 1 0 1 0 0 1 0 0 1 1 0 1 1
1 1 1 1 1 1 1 1 1 1 1 1 1 1 1 1 0 1 1 0 1 1 1 1 1 1 1 1
0 0 0 0 0 0 0 0 0 0 0 0 0 0 0 0 0 1 1 0 0 0 0 0 0 0 0 0
1 1 1 1 0 0 1 1 1 0 1 0 0 0 1 1 0 1 1 0 1 1 0 1 0 1 1 0
1 0 1 0 0 0 1 1 0 0 1 1 0 0 1 1 0 1 1 0 0 1 0 1 1 0 1 0
0 0 1 0 0 0 1 0 0 0 1 0 0 0 0 1 0 1 0 0 1 1 1 0 0 1 0 0
0 0 1 1 0 0 0 1 1 0 1 1 0 0 1 1 0 1 1 0 1 1 1 0 0 1 1 0
1 0 1 1 0 1 1 1 0 1 1 1 1 0 1 1 0 1 0 0 1 0 0 1 1 0 1 1
0 0 0 0 0 0 1 1 0 0 1 1 0 0 1 1 0 1 1 0 0 0 0 1 1 0 1 0
*/
